// Logisim project SimpleCpu.circ as structural Verilog: 3 circuits, main circuit MyALU
module MyALU (
  input  [7:0] InA,
  input  [7:0] InB,
  input  Asen,
  output [7:0] Result
);

  wire [7:0] adder_1_out, subtractor_1_out;

  Adder adder_1 (.a(InA), .b(InB), .out(adder_1_out));  // open: cin, cout
  Subtractor subtractor_1 (.a(InA), .b(InB), .out(subtractor_1_out));  // open: bin, bout
  Multiplexer #(.width(8), .enable("false")) multiplexer_1 (
    .in0(adder_1_out), .in1(subtractor_1_out), .out(Result), .sel(Asen));
endmodule

module ControlUnit (
  input  Clock,
  input  Reset,
  input  [1:0] OpCode,
  output IRin,
  output Rxin,
  output Rxout,
  output Ryout,
  output Ain,
  output Bin,
  output Bout,
  output DINout,
  output Asen,
  output DONE
);

  wire and_1_out, and_2_out, and_3_out, and_4_out, and_5_out, and_6_out, and_7_out, and_8_out, and_9_out,
       and_10_out, and_11_out, and_12_out, and_13_out, and_14_out, and_15_out, and_16_out, decoder_1_out0,
       decoder_1_out1, decoder_1_out2, decoder_1_out3, decoder_2_out1, decoder_2_out2, decoder_2_out3,
       or_1_out, or_2_out;
  wire [1:0] counter_1_q;

  Decoder #(.select(2), .enable("false")) decoder_1 (
    .out0(decoder_1_out0), .out1(decoder_1_out1), .out2(decoder_1_out2), .out3(decoder_1_out3), .sel(OpCode));
  and and_1 (and_1_out, decoder_1_out0, decoder_2_out1);
  Counter #(.width(2), .max('h3)) counter_1 (
    .load(or_1_out), .D(2'b00), .Q(counter_1_q), .clk(Clock), .clr(Reset));  // open: count, carry
  or or_1 (or_1_out, DINout, and_1_out);
  Decoder #(.select(2), .enable("false")) decoder_2 (
    .out0(IRin), .out1(decoder_2_out1), .out2(decoder_2_out2), .out3(decoder_2_out3), .sel(counter_1_q));
  and and_2 (and_2_out, decoder_1_out2, decoder_2_out3);
  and and_3 (and_3_out, decoder_1_out3, decoder_2_out3);
  and and_4 (and_4_out, decoder_1_out0, decoder_2_out1);
  and and_5 (and_5_out, decoder_1_out1, decoder_2_out1);
  and and_6 (and_6_out, decoder_1_out2, decoder_2_out3);
  and and_7 (and_7_out, decoder_2_out3, decoder_1_out3);
  and and_8 (and_8_out, decoder_1_out2, decoder_2_out1);
  and and_9 (and_9_out, decoder_1_out3, decoder_2_out1);
  and and_10 (and_10_out, decoder_1_out0, decoder_2_out1);
  and and_11 (and_11_out, decoder_1_out2, decoder_2_out2);
  and and_12 (and_12_out, decoder_1_out3, decoder_2_out2);
  and and_13 (and_13_out, decoder_1_out2, decoder_2_out2);
  and and_14 (and_14_out, decoder_2_out2, decoder_1_out3);
  and and_15 (and_15_out, decoder_1_out2, decoder_2_out3);
  and and_16 (and_16_out, decoder_2_out3, decoder_1_out3);
  and and_17 (DINout, decoder_1_out1, decoder_2_out1);
  and and_18 (Asen, decoder_1_out3, decoder_2_out2);
  or or_2 (or_2_out, and_2_out, and_3_out);
  or or_3 (Ain, and_8_out, and_9_out);
  or or_4 (Bin, and_13_out, and_14_out);
  or or_5 (Bout, and_15_out, and_16_out);
  or or_6 (Rxin, and_4_out, and_5_out, and_6_out, and_7_out);
  or or_7 (Ryout, and_10_out, and_11_out, and_12_out);
  or or_8 (DONE, or_2_out, or_1_out);

  assign Rxout = Ain;
endmodule

module CPU (
  input  [7:0] DIN
);

  wire Clock_out, controlunit_1_ain, controlunit_1_asen, controlunit_1_bin, controlunit_1_bout,
       controlunit_1_dinout, controlunit_1_irin, controlunit_1_rxout, controlunit_1_ryout, decoder_1_out0,
       decoder_1_out1, decoder_1_out2, decoder_1_out3, decoder_1_out4, decoder_1_out5, decoder_1_out6,
       decoder_1_out7, Reset_out;
  wire [7:0] A_q, B_q, controlled_buffer_1_out, IR_q, multiplexer_1_out, multiplexer_2_out, myalu_1_result,
       R0_q, R1_q, R2_q, R3_q, R4_q, R5_q, R6_q, R7_q;

  assign controlled_buffer_1_out = controlunit_1_dinout ? DIN : 8'bz;  // Controlled_Buffer controlled_buffer_1
  Button Reset (.out(Reset_out));
  Clock Clock (.out(Clock_out));
  Decoder #(.select(3)) decoder_1 (
    .out0(decoder_1_out0), .out1(decoder_1_out1), .out2(decoder_1_out2), .out3(decoder_1_out3),
    .out4(decoder_1_out4), .out5(decoder_1_out5), .out6(decoder_1_out6), .out7(decoder_1_out7),
    .sel(IR_q[5:3]));  // open: en
  Register IR (.D(DIN), .en(controlunit_1_irin), .Q(IR_q), .clk(Clock_out), .clr(Reset_out));
  // Probe on controlled_buffer_1_out
  Register R0 (.D(controlled_buffer_1_out), .en(decoder_1_out0), .Q(R0_q), .clk(Clock_out), .clr(Reset_out));
  Register R1 (.D(controlled_buffer_1_out), .en(decoder_1_out1), .Q(R1_q), .clk(Clock_out), .clr(Reset_out));
  Register R2 (.D(controlled_buffer_1_out), .en(decoder_1_out2), .Q(R2_q), .clk(Clock_out), .clr(Reset_out));
  Register R3 (.D(controlled_buffer_1_out), .en(decoder_1_out3), .Q(R3_q), .clk(Clock_out), .clr(Reset_out));
  Register R4 (.D(controlled_buffer_1_out), .en(decoder_1_out4), .Q(R4_q), .clk(Clock_out), .clr(Reset_out));
  Register R5 (.D(controlled_buffer_1_out), .en(decoder_1_out5), .Q(R5_q), .clk(Clock_out), .clr(Reset_out));
  Register R6 (.D(controlled_buffer_1_out), .en(decoder_1_out6), .Q(R6_q), .clk(Clock_out), .clr(Reset_out));
  Register R7 (.D(controlled_buffer_1_out), .en(decoder_1_out7), .Q(R7_q), .clk(Clock_out), .clr(Reset_out));
  ControlUnit controlunit_1 (
    .Clock(Clock_out), .Reset(Reset_out), .OpCode(IR_q[7:6]), .IRin(controlunit_1_irin),
    .Rxout(controlunit_1_rxout), .Ryout(controlunit_1_ryout), .Ain(controlunit_1_ain),
    .Bin(controlunit_1_bin), .Bout(controlunit_1_bout), .DINout(controlunit_1_dinout),
    .Asen(controlunit_1_asen));  // open: Rxin, DONE
  Multiplexer #(.select(3), .width(8), .enable("false")) multiplexer_1 (
    .in0(R0_q), .in1(R1_q), .in2(R2_q), .in3(R3_q), .in4(R4_q), .in5(R5_q), .in6(R6_q), .in7(R7_q),
    .out(multiplexer_1_out), .sel(IR_q[5:3]));
  Multiplexer #(.select(3), .width(8), .enable("false")) multiplexer_2 (
    .in0(R0_q), .in1(R1_q), .in2(R2_q), .in3(R3_q), .in4(R4_q), .in5(R5_q), .in6(R6_q), .in7(R7_q),
    .out(multiplexer_2_out), .sel(IR_q[2:0]));
  Register A (.D(controlled_buffer_1_out), .en(controlunit_1_ain), .Q(A_q), .clk(Clock_out), .clr(Reset_out));
  assign controlled_buffer_1_out = controlunit_1_bout ? B_q : 8'bz;  // Controlled_Buffer controlled_buffer_2
  assign controlled_buffer_1_out = controlunit_1_rxout ? multiplexer_1_out : 8'bz;  // Controlled_Buffer controlled_buffer_3
  assign controlled_buffer_1_out = controlunit_1_ryout ? multiplexer_2_out : 8'bz;  // Controlled_Buffer controlled_buffer_4
  MyALU myalu_1 (.InA(A_q), .InB(controlled_buffer_1_out), .Asen(controlunit_1_asen), .Result(myalu_1_result));
  Register B (.D(myalu_1_result), .en(controlunit_1_bin), .Q(B_q), .clk(Clock_out), .clr(Reset_out));
endmodule
